// Logisim project muplex_8in.circ as structural Verilog: 1 circuit, main circuit main
module main (
);

  wire _1_2_out, _1_3_out, _1_out, _2_2_out, _2_3_out, _2_out, _3_2_out, _3_out, _4_2_out, _4_out, _5_out,
       _6_out, _7_out, _8_out, not_1_out, not_2_out, not_3_out, not_4_out, not_5_out, not_6_out, not_7_out,
       or_1_out, or_2_out, or_3_out, undriven, undriven_2, undriven_3, undriven_4, undriven_5, undriven_6,
       undriven_7, undriven_8, undriven_9, undriven_10, undriven_11, undriven_12, undriven_13, undriven_14,
       undriven_15, undriven_16, undriven_17, undriven_18, undriven_19, undriven_20;

  not not_1 (not_1_out, undriven_10);
  not not_2 (not_2_out, undriven_9);
  not not_3 (not_3_out, undriven_11);
  and _1 (_1_out, undriven, not_2_out, not_1_out, not_3_out);
  and _2 (_2_out, undriven_2, not_2_out, not_1_out, undriven_11);
  and _3 (_3_out, undriven_3, not_2_out, undriven_10, not_3_out);
  and _4 (_4_out, undriven_4, not_2_out, undriven_10, undriven_11);
  and _5 (_5_out, undriven_5, undriven_9, not_1_out, not_3_out);
  and _6 (_6_out, undriven_6, undriven_9, not_1_out, undriven_11);
  and _7 (_7_out, undriven_7, undriven_9, undriven_10, not_3_out);
  and _8 (_8_out, undriven_8, undriven_9, undriven_10);
  or or_1 (or_1_out, _1_out, _2_out, _3_out, _4_out, _5_out, _6_out, _7_out, _8_out);
  not not_4 (not_4_out, undriven_18);
  not not_5 (not_5_out, undriven_19);
  and _1_2 (_1_2_out, undriven_16, undriven_19);
  and _2_2 (_2_2_out, undriven_17, not_5_out);
  not not_6 (not_6_out, undriven_20);
  not not_7 (not_7_out, undriven_20);
  and _1_3 (_1_3_out, undriven_12, not_4_out, not_6_out);
  and _2_3 (_2_3_out, undriven_13, not_4_out, undriven_20);
  and _3_2 (_3_2_out, undriven_14, undriven_18, not_7_out);
  and _4_2 (_4_2_out, undriven_15, undriven_18, undriven_20);
  or or_2 (or_2_out, _1_2_out, _2_2_out);
  or or_3 (or_3_out, _1_3_out, _2_3_out, _3_2_out, _4_2_out);

  // Notes on the sheet:
  //   I0
  //   I1
  //   I2
  //   I3
  //   I4
  //   I5
  //   I6
  //   I7
  //   S2
  //   S0
  //   S1
  //   Mutex 8in
  //   Z
  //   I0
  //   I1
  //   I0
  //   I1
  //   I2
  //   I3
  //   S0
  //   S1
  //   S0
  //   Mutex 2in
  //   Mutex 4in
  //   Z
  //   Z
endmodule
