// Logisim project muplex_8in_v2.circ as structural Verilog: 1 circuit, main circuit main
module main (
);

  wire _1_2_out, _1_3_out, _1_4_out, _1_5_out, _1_6_out, _1_out, _2_2_out, _2_3_out, _2_4_out, _2_5_out,
       _2_6_out, _2_out, _3_2_out, _3_3_out, _3_4_out, _3_out, _4_2_out, _4_3_out, _4_4_out, _4_out, _5_out,
       _6_out, _7_out, _8_out, not_1_out, not_2_out, not_3_out, not_4_out, not_5_out, not_6_out, not_7_out,
       not_8_out, not_9_out, not_10_out, not_11_out, not_12_out, not_13_out, not_14_out, or_1_out, or_2_out,
       or_3_out, or_4_out, or_5_out, or_6_out, undriven, undriven_2, undriven_3, undriven_4, undriven_5,
       undriven_6, undriven_7, undriven_8, undriven_9, undriven_10, undriven_11, undriven_12, undriven_13,
       undriven_14, undriven_15, undriven_16, undriven_17, undriven_18, undriven_19, undriven_20,
       undriven_21, undriven_22, undriven_23, undriven_24, undriven_25, undriven_26, undriven_27,
       undriven_28, undriven_29, undriven_30, undriven_31, undriven_32, undriven_33;

  not not_1 (not_1_out, undriven_10);
  not not_2 (not_2_out, undriven_9);
  not not_3 (not_3_out, undriven_11);
  and _1 (_1_out, undriven, not_2_out, not_1_out, not_3_out);
  and _2 (_2_out, undriven_2, not_2_out, not_1_out, undriven_11);
  and _3 (_3_out, undriven_3, not_2_out, undriven_10, not_3_out);
  and _4 (_4_out, undriven_4, not_2_out, undriven_10, undriven_11);
  and _5 (_5_out, undriven_5, undriven_9, not_1_out, not_3_out);
  and _6 (_6_out, undriven_6, undriven_9, not_1_out, undriven_11);
  and _7 (_7_out, undriven_7, undriven_9, undriven_10, not_3_out);
  and _8 (_8_out, undriven_8, undriven_9, undriven_10);
  or or_1 (or_1_out, _1_out, _2_out, _3_out, _4_out, _5_out, _6_out, _7_out, _8_out);
  not not_4 (not_4_out, undriven_18);
  not not_5 (not_5_out, undriven_19);
  and _1_2 (_1_2_out, undriven_16, undriven_19);
  and _2_2 (_2_2_out, undriven_17, not_5_out);
  not not_6 (not_6_out, undriven_20);
  not not_7 (not_7_out, undriven_20);
  not not_8 (not_8_out, undriven_30);
  not not_9 (not_9_out, undriven_29);
  and _1_3 (_1_3_out, undriven_12, not_4_out, not_6_out);
  and _2_3 (_2_3_out, undriven_13, not_4_out, undriven_20);
  and _3_2 (_3_2_out, undriven_14, undriven_18, not_7_out);
  and _4_2 (_4_2_out, undriven_15, undriven_18, undriven_20);
  not not_10 (not_10_out, undriven_32);
  not not_11 (not_11_out, undriven_32);
  not not_12 (not_12_out, undriven_31);
  not not_13 (not_13_out, undriven_31);
  or or_2 (or_2_out, _1_2_out, _2_2_out);
  or or_3 (or_3_out, _1_3_out, _2_3_out, _3_2_out, _4_2_out);
  and _1_4 (_1_4_out, undriven_25, not_8_out, not_10_out);
  and _2_4 (_2_4_out, undriven_26, not_8_out, undriven_32);
  and _3_3 (_3_3_out, undriven_27, undriven_30, not_11_out);
  and _4_3 (_4_3_out, undriven_28, undriven_30, undriven_32);
  and _1_5 (_1_5_out, undriven_21, not_9_out, not_12_out);
  and _2_5 (_2_5_out, undriven_22, not_9_out, undriven_31);
  and _3_4 (_3_4_out, undriven_23, undriven_29, not_13_out);
  and _4_4 (_4_4_out, undriven_24, undriven_29, undriven_31);
  or or_4 (or_4_out, _1_5_out, _2_5_out, _3_4_out, _4_4_out);
  or or_5 (or_5_out, _1_4_out, _2_4_out, _3_3_out, _4_3_out);
  not not_14 (not_14_out, undriven_33);
  and _1_6 (_1_6_out, or_5_out, undriven_33);
  and _2_6 (_2_6_out, or_4_out, not_14_out);
  or or_6 (or_6_out, _1_6_out, _2_6_out);

  // Notes on the sheet:
  //   I0
  //   I1
  //   I2
  //   I3
  //   I4
  //   I5
  //   I6
  //   I7
  //   S2
  //   S0
  //   S1
  //   Mutex 8in
  //   Z
  //   I0
  //   I1
  //   I0
  //   I1
  //   I2
  //   I3
  //   S0
  //   S1
  //   S0
  //   I0
  //   I1
  //   I2
  //   I3
  //   I0
  //   I1
  //   I2
  //   I3
  //   Mutex 2in
  //   Mutex 4in
  //   S1
  //   S3
  //   S2
  //   Mutex 4in
  //   S0
  //   Mutex 4in
  //   Z
  //   Z
  //   S4
  //   Mutex 2in
  //   Z
endmodule
